// Logisim project Assignment 1.circ as structural Verilog: 1 circuit, main circuit main
module main (
  input  in_1,
  input  C,
  input  A,
  input  D,
  input  B,
  input  E,
  input  C_2,
  input  D_2,
  input  E_2,
  input  A_2,
  input  B_2
);

  wire transistor_1_out, transistor_2_out, transistor_5_out, transistor_6_out, transistor_7_out;

  Transistor transistor_1 (.in(in_1), .out(transistor_1_out), .gate(A));
  Transistor transistor_2 (.in(transistor_1_out), .out(transistor_2_out), .gate(B));
  Transistor #(.\type ("n")) transistor_3 (.in(transistor_5_out), .out(transistor_2_out), .gate(C_2));
  Transistor #(.\type ("n")) transistor_4 (.in(transistor_5_out), .out(transistor_2_out), .gate(D_2));
  Transistor #(.\type ("n")) transistor_5 (.in(1'b0), .out(transistor_5_out), .gate(A_2));
  Transistor transistor_6 (.in(in_1), .out(transistor_6_out), .gate(C));
  Transistor transistor_7 (.in(transistor_6_out), .out(transistor_7_out), .gate(D));
  Transistor transistor_8 (.in(transistor_7_out), .out(transistor_2_out), .gate(E));
  Transistor #(.\type ("n")) transistor_9 (.in(transistor_5_out), .out(transistor_2_out), .gate(E_2));
  Transistor #(.\type ("n")) transistor_10 (.in(1'b0), .out(transistor_5_out), .gate(B_2));

  // Notes on the sheet:
  //   VDD
  //   GND
  //   Y=((A+B).(C+D+E))'
endmodule
